# Fritzing sketch project-sketch (saved by Fritzing 0.8.5b)

parts:
  IOIO-OTG = IOIO for Android
  Front_Motor_Controller = motorcontrollerDRI0002
  Back_Motor_Controller = motorcontrollerDRI0002
  Grasp_&_Wrist = TB6612FNG Breakout v11
  Elbow_&_Sholder = TB6612FNG Breakout v11
  Turn_&_Led = TB6612FNG Breakout v11
  M1 = DC Motor
  M2 = DC Motor
  M3 = DC Motor
  M4 = DC Motor
  Grasp_Motor = DC Motor
  Wrist_Motor = DC Motor
  Arm_Remote_Connector = Header 8 [package=1x08_smd_alt]
  D-cell_x4 = 4 x AAA Battery Mount
  LED2 = LEDs [package=led10mm]
  Elbow = DC Motor
  Sholder = DC Motor
  Turn = DC Motor
  6_AAA = 4 x AAA Battery Mount
  U1 = SWITCH_SPDT [package=kps-1290]
  J1 = Power Jack [package=power_jack_pth]
  STANDBY_parallel_split = MMA_ACCEL_CONNECTOR [package=1x08]
  PWM_paralel_split = MMA_ACCEL_CONNECTOR [package=1x08]
  R1 = Rotary Potentiometer (Large) [maximum_resistance=100kΩ package=THT]
  R2 = Rotary Potentiometer (Large) [maximum_resistance=100kΩ package=THT]
  R3 = Rotary Potentiometer (Large) [maximum_resistance=100kΩ package=THT]
  U5 = MMA_ACCEL_CONNECTOR [package=1x08]
  U7 = MMA_ACCEL_CONNECTOR [package=1x08]
  U6 = MMA_ACCEL_CONNECTOR [package=1x08]
  VCC1 = Battery block 9V

nets:
  N1: IOIO-OTG.PIN19, Turn_&_Led.AIN2
  N2: IOIO-OTG.3.3V, U7.SLP
  N3: IOIO-OTG.VCC, VCC1.+
  N4: IOIO-OTG.GND, U6.SLP, VCC1.-
  N5: IOIO-OTG.PIN46, Back_Motor_Controller.E2
  N6: IOIO-OTG.PIN45, Back_Motor_Controller.E1
  N7: IOIO-OTG.PIN44, Back_Motor_Controller.M2
  N8: IOIO-OTG.PIN43, Back_Motor_Controller.M1
  N9: IOIO-OTG.PIN42, Front_Motor_Controller.M2
  N10: IOIO-OTG.PIN41, Front_Motor_Controller.M1
  N11: IOIO-OTG.PIN40, Front_Motor_Controller.E2
  N12: IOIO-OTG.PIN39, Front_Motor_Controller.E1
  N13: IOIO-OTG.PIN33, Grasp_&_Wrist.BIN2
  N14: IOIO-OTG.PIN32, Grasp_&_Wrist.BIN1
  N15: IOIO-OTG.PIN31, STANDBY_parallel_split.VCC
  N16: IOIO-OTG.PIN30, Grasp_&_Wrist.AIN2
  N17: IOIO-OTG.PIN29, Grasp_&_Wrist.AIN1
  N18: IOIO-OTG.PIN28, PWM_paralel_split.VCC
  N19: IOIO-OTG.PIN26, Elbow_&_Sholder.AIN2
  N20: IOIO-OTG.PIN25, Elbow_&_Sholder.AIN1
  N21: IOIO-OTG.PIN24, Elbow_&_Sholder.BIN1
  N22: IOIO-OTG.PIN23, Elbow_&_Sholder.BIN2
  N23: IOIO-OTG.PIN22, Turn_&_Led.BIN2
  N24: IOIO-OTG.PIN21, Turn_&_Led.BIN1
  N25: IOIO-OTG.PIN20, Turn_&_Led.AIN1
  GND: Front_Motor_Controller.GND, Back_Motor_Controller.GND, U1.P
  N26: Front_Motor_Controller.VS, Back_Motor_Controller.VS, 6_AAA.-, J1.GND
  N27: Front_Motor_Controller.M1-, M3.pin_2
  N28: Front_Motor_Controller.M1+, M3.pin_1
  N29: Front_Motor_Controller.M2+, M1.pin_1
  N30: Front_Motor_Controller.M2-, M1.pin_2
  N31: Back_Motor_Controller.M1-, M2.pin_2
  N32: Back_Motor_Controller.M1+, M2.pin_1
  N33: Back_Motor_Controller.M2+, M4.pin_1
  N34: Back_Motor_Controller.M2-, M4.pin_2
  GND_2: Grasp_&_Wrist.GND, Elbow_&_Sholder.GND, Turn_&_Led.GND, Arm_Remote_Connector.-, D-cell_x4.-
  N35: Grasp_&_Wrist.B01, Wrist_Motor.pin_1, Arm_Remote_Connector.2
  N36: Grasp_&_Wrist.A01, Grasp_Motor.pin_1, Arm_Remote_Connector.1
  N37: Grasp_&_Wrist.VM, Elbow_&_Sholder.VM, Turn_&_Led.VM, Arm_Remote_Connector.+, D-cell_x4.+
  N38: Grasp_&_Wrist.PWMA, PWM_paralel_split.GS2
  N39: Grasp_&_Wrist.STBY, STANDBY_parallel_split.SLP
  N40: Grasp_&_Wrist.PWMB, PWM_paralel_split.SLP
  N41: Elbow_&_Sholder.B02, Arm_Remote_Connector.4, Sholder.pin_1
  N42: Elbow_&_Sholder.A01, Arm_Remote_Connector.3, Elbow.pin_1
  N43: Elbow_&_Sholder.PWMA, PWM_paralel_split.Z
  N44: Elbow_&_Sholder.STBY, STANDBY_parallel_split.GS2
  N45: Elbow_&_Sholder.PWMB, PWM_paralel_split.GS1
  N46: Turn_&_Led.B01, Arm_Remote_Connector.5, Turn.pin_1
  N47: Turn_&_Led.A01, Arm_Remote_Connector.6, LED2.A
  N48: Turn_&_Led.STBY, STANDBY_parallel_split.GS1
  N49: Turn_&_Led.PWMB, PWM_paralel_split.Y
  N50: Grasp_Motor.pin_2, Wrist_Motor.pin_2, Elbow.pin_2
  N51: Sholder.pin_2, Turn.pin_2
  N52: 6_AAA.+, U1.O
  N53: U1.S, J1.PWR
  N54: R1.leg1, R2.leg1, R3.leg1, U6.VCC
  N55: R1.wiper, U5.GND
  N56: R2.wiper, U5.VCC
  N57: R2.leg2, U7.VCC
  N58: R3.wiper, U5.X

notes:
  ROB0003 Chassis
  Robotic Arm Edgw
  this part is encapsulated inside the arrm
  Close-Loop Potentiometers monitoring

custom parts:
  Header 8: Header 8 Standard 8-pin 0.1 header. Use with straight break away headers (SKU : PRT-00116), right angle break away headers (PRT-00553), swiss pins (PRT-00743), machine pins (PRT-00117), and female headers (PRT-00115).
